# Fritzing sketch robotikaProjekt (saved by Fritzing 0.9.9b)
breadboards: 1

parts:
  Part1 = Arduino Micro (Rev3)
  PIR1 = PIR sensor
  J1 = Piezo Speaker
  R1 = Resistor [tolerance=±5% resistance=220 package="0603 [SMD]"]
  LED1 = LED - 5mm [color="Red (633nm)" current=0.030 package="5 mm [THT]"]
  LED2 = LED - 5mm [color="Green (570nm)" current=0.030 package="5 mm [THT]"]
  R2 = Resistor [tolerance=±5% resistance=220 package="1206 [SMD]"]
  Part2 = LCD1602-I2C

nets:
  GND: Part1.GND, PIR1.GND, J1.pin1, LED1.cathode, LED2.cathode, Part2.GND
  N1: Part1.D2/SDA, Part2.SDA
  N2: Part1.D3/SCL, Part2.SCL
  N3: Part1.D8_PWM/A8, Part1.D11_PWM, J1.pin2
  N4: Part1.D9_PWM/A9, R1.Pin_0
  N5: Part1.D10_PWM/A10, R2.Pin_0
  N6: Part1.D12_PWM/A11, PIR1.SIG
  5V: Part1.5V, PIR1.VDD, Part2.VCC
  N7: R1.Pin_1, LED1.anode
  N8: LED2.anode, R2.Pin_1

custom parts:
  LCD1602-I2C: A standard character display, usually with 2x16 characters. Comes in many colors with LCM1602 IIC attached.
